# Fritzing sketch pendance (saved by Fritzing 0.9.2b)
breadboards: 1

parts:
  Promini = Arduino Pro Mini v13
  S2 = Pushbutton [package="[THT]"]
  S3 = Toggle Switch [package=THT]
  R1 = Resistor [tolerance=±5% resistance=4.7k package=THT]
  S4 = Pushbutton [package="[THT]"]
  R2 = Resistor [tolerance=±5% resistance=4.7k package=THT]
  R3 = Resistor [tolerance=±5% resistance=4.7k package=THT]
  R4 = Resistor [tolerance=±5% resistance=4.7k package=THT]
  Q1 = NPN-Transistor [package="TO92 [THT]"]
  U1 = Vibration Motor- ROB-08449 [package=vibe-motor-10mm]

nets:
  GND: Promini.GND, S2.Pin_1, S2.Pin_2, S3.COM, S4.Pin_1, S4.Pin_2, Q1.E
  3.7V: Promini.RAW, Promini.D8, Promini.D7, Promini.D3_PWM, Promini.D2, R1.Pin_0, R2.Pin_0, R3.Pin_0, R4.Pin_0, U1.+
  N1: Promini.D9_PWM, Q1.B
  N2: S2.Pin_3, S2.Pin_4, R1.Pin_1
  N3: S3.L1, R4.Pin_1
  N4: S3.L2, R3.Pin_1
  N5: S4.Pin_3, S4.Pin_4, R2.Pin_1
